# Fritzing sketch Mischencontroll (saved by Fritzing 0.9.3b)
breadboards: 1

parts:
  Part1 = Arduino Mega ADK (Rev3)
  R1 = Rotary Potentiometer (Small) [maximum_resistance=100kΩ package=THT]
  S1 = Toggle Switch [package=THT]
  LCM1602_IIC2 = LCM1602 IIC [part_number="LCM1602 IIC" chip_label="LCM1602 IIC" package="DIP (Dual Inline) [THT]"]
  LCD1 = LCD screen
  SparkFun_Load_Cell_Amplifier_-_HX1 = SparkFun Load Cell Amplifier - HX711 [part_number=SEN-13879]
  Load_Cell1 = Load Cell - Red/white/black/green
  KY-1 = Keyes Relay [package=THT]
  KY-2 = Keyes Relay [package=THT]
  BAT1 = BC9VPC [package=bc9vpc]
  M1 = DC Motor
  M2 = DC Motor
  S2 = Pushbutton [package="[SMD]"]
  R2 = Rotary Potentiometer (Small) [maximum_resistance=100kΩ package=THT]
  S3 = Pushbutton [package="[SMD]"]
  S4 = Pushbutton [package="[SMD]"]
  R3 = Resistor [tolerance=±5% resistance=220 package=THT]
  R4 = Resistor [tolerance=±5% resistance=220 package=THT]
  R5 = Resistor [tolerance=±5% resistance=220 package=THT]

nets:
  N1: Part1.A9, R2.wiper
  N2: Part1.A5, R1.wiper
  N3: Part1.D21/SCL, LCM1602_IIC2.SCL
  N4: Part1.D20/SDA, LCM1602_IIC2.SDA
  N5: Part1.D12_PWM, Part1.D11_PWM, Part1.D10_PWM, S1.COM, KY-1.power, KY-2.power, S2.Pin_1, S2.Pin_2, S3.Pin_1, S3.Pin_2, S4.Pin_1, S4.Pin_2
  5V: Part1.5V, R1.leg2, S1.L2, LCM1602_IIC2.VCC, SparkFun_Load_Cell_Amplifier_-_HX1.VDD, R2.leg2
  GND: Part1.GND, R1.leg1, LCM1602_IIC2.GND, SparkFun_Load_Cell_Amplifier_-_HX1.GND, Load_Cell1.wire3, KY-1.ground, KY-2.ground, R2.leg1, R3.Pin_0, R4.Pin_0, R5.Pin_0
  N6: Part1.D2_PWM, SparkFun_Load_Cell_Amplifier_-_HX1.SCK
  N7: Part1.D3_PWM, SparkFun_Load_Cell_Amplifier_-_HX1.DAT
  N8: Part1.D4_PWM, KY-1.signal
  N9: Part1.D5_PWM, KY-2.signal
  VSS: LCM1602_IIC2.VSS, LCD1.VSS
  VDD: LCM1602_IIC2.VDD, LCD1.VDD
  N10: LCM1602_IIC2.V0, LCD1.V0
  N11: LCM1602_IIC2.RS, LCD1.RS
  N12: LCM1602_IIC2.RW, LCD1.R/W
  N13: LCM1602_IIC2.E, LCD1.E
  N14: LCM1602_IIC2.D0, LCD1.DB0
  N15: LCM1602_IIC2.D1, LCD1.DB1
  N16: LCM1602_IIC2.D2, LCD1.DB2
  N17: LCM1602_IIC2.D3, LCD1.DB3
  N18: LCM1602_IIC2.D4, LCD1.DB4
  N19: LCM1602_IIC2.D5, LCD1.DB5
  N20: LCM1602_IIC2.D6, LCD1.DB6
  N21: LCM1602_IIC2.D7, LCD1.DB7
  N22: LCM1602_IIC2.A, LCD1.LED+
  N23: LCM1602_IIC2.K, LCD1.LED-
  N24: LCM1602_IIC2.LED_A, LCM1602_IIC2.LED_B
  N25: SparkFun_Load_Cell_Amplifier_-_HX1.A+, Load_Cell1.wire4
  N26: SparkFun_Load_Cell_Amplifier_-_HX1.A-, Load_Cell1.wire2
  N27: SparkFun_Load_Cell_Amplifier_-_HX1.AVDD, Load_Cell1.wire1
  N28: KY-1.C, M1.pin_1
  N29: KY-1.NO, KY-2.NO, BAT1.V+
  N30: KY-2.C, M2.pin_1
  N31: BAT1.V-, M1.pin_2, M2.pin_2
  N32: S2.Pin_3, S2.Pin_4, R3.Pin_1
  N33: S3.Pin_3, S3.Pin_4, R4.Pin_1
  N34: S4.Pin_3, S4.Pin_4, R5.Pin_1

custom parts:
  LCM1602 IIC: I2C-Module to use a 1602 or 2004 LCD on with the wire.h libory Serial LCD Modul
  SparkFun Load Cell Amplifier - HX711: The SparkFun Load Cell Amplifier is a small breakout board for the HX711 IC that allows you to easily read load cells to measure weight. By connecting the amplifier to your microcontroller you will be able to read the changes in the resistance of the load cell, and with some calibration you’ll be able to get very accurate weight measurements. This can be handy for creating your own industrial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
  Load Cell - Red/white/black/green: A rectangle load cell/weighting pressure Sensor with four wires - Red, white, black, green. Normally corresponding with E+, E-, A+, A- respectively.
  Keyes Relay: The Keyes 5V relay module is suitable for SCM development, home appliance control. It uses a 5V~12V TIL control signal which can control DC / AC signal.
